# Fritzing sketch humidity_tank_wiring (saved by Fritzing 0.9.3b)

parts:
  WeMos_D1_Mini1 = WeMos D1 Mini
  HX711 = HX711 Weighing Sensor Module
  Lower_Left = Load Sensor - 50kg [part_number=SEN-10245]
  Upper_Right = Load Sensor - 50kg [part_number=SEN-10245]
  Lower_Right = Load Sensor - 50kg [part_number=SEN-10245]
  Upper_Left = Load Sensor - 50kg [part_number=SEN-10245]

nets:
  5V: WeMos_D1_Mini1.5V, HX711.VCC
  N1: WeMos_D1_Mini1.D1, HX711.CK/TX
  N2: WeMos_D1_Mini1.D2, HX711.DO/RX
  N3: WeMos_D1_Mini1.G, HX711.GND
  N4: HX711.E+, Lower_Right.R
  N5: HX711.E-, Upper_Left.R
  N6: HX711.A+, Upper_Right.R
  N7: HX711.A-, Lower_Left.R
  N8: Lower_Left.B, Upper_Left.B
  N9: Lower_Left.W, Lower_Right.W
  N10: Upper_Right.B, Lower_Right.B
  N11: Upper_Right.W, Upper_Left.W

custom parts:
  Load Sensor - 50kg: Half-wheatstone bridge Load Cell modified from the Fritzing Repo This load sensor, sometimes called a strain gauge, is the same one found in digital bathroom scales (you know, the ones you use in January for your New Year's resolutions, and then forget about a month later). This sensor can measure up to about 110 pounds.
